# Fritzing sketch lcm1602-i2c-leds (saved by Fritzing 0.9.6b)
breadboards: 1

parts:
  Part1 = Arduino Mega 2560 (Rev3)
  LCM1602_IIC3 = LCM1602 IIC [part_number="LCM1602 IIC" chip_label="LCM1602 IIC" package="DIP (Dual Inline) [THT]"]
  LED1 = LED - 5mm [color="Red (633nm)" current=0.030 package="5 mm [THT]"]
  R1 = Resistor [tolerance=±5% power=0.25 resistance=220 package=THT]

nets:
  N1: Part1.D21/SCL, LCM1602_IIC3.SCL
  N2: Part1.D20/SDA, LCM1602_IIC3.SDA
  5V: Part1.5V, LCM1602_IIC3.VCC
  GND: Part1.GND, LCM1602_IIC3.GND, R1.Pin_1
  N3: LCM1602_IIC3.D0, LED1.anode
  N4: LED1.cathode, R1.Pin_0

custom parts:
  LCM1602 IIC: I2C-Module to use a 1602 or 2004 LCD on with the wire.h libory Serial LCD Modul
